# Fritzing sketch servo (saved by Fritzing 0.6.3b)
stripboards: 1

parts:
  Arduino1 = Arduino
  J1 = Basic Servo
  J2 = Basic Servo
  J3 = Basic Servo
  J4 = Basic Servo
  J5 = Basic Servo
  VCC1 = Battery block 9V
  Part1 = Bluetooth Mate Silver

nets:
  GND: Arduino1.GND, J1.gnd, J2.gnd, J3.gnd, J4.gnd, J5.gnd, VCC1.-, Part1.GND
  N1: Arduino1.D11, J1.pulse
  N2: Arduino1.D9, J3.pulse
  N3: Arduino1.D5, J4.pulse
  N4: Arduino1.D3, J5.pulse
  N5: Arduino1.D1TX, Part1.RX_5V
  N6: Arduino1.D0RX, Part1.TX_5V
  +5V: Arduino1.+5V, Part1.VCC
  VCC: J1.vcc, J2.vcc, J3.vcc, J4.vcc, J5.vcc, VCC1.+
